# Fritzing sketch rfid (saved by Fritzing 0.9.3b)
circuit board: 8.46667cm x 5.64444cm
breadboards: 1

parts:
  Gizwits_WiFi_Witty_ESP-12F1 = Gizwits WiFi Witty ESP-12F
  Part1 = RFID-RC522-v2
  Power_plug1 = Power plug

nets:
  N1: Gizwits_WiFi_Witty_ESP-12F1.GPIO14, Part1.SCK
  N2: Gizwits_WiFi_Witty_ESP-12F1.GPIO12, Part1.MISO
  N3: Gizwits_WiFi_Witty_ESP-12F1.GPIO13, Part1.MOSI
  VCC: Gizwits_WiFi_Witty_ESP-12F1.VCC, Part1.3.3V, Power_plug1.VCC
  GND: Gizwits_WiFi_Witty_ESP-12F1.GND, Part1.GND, Power_plug1.GND
  N4: Gizwits_WiFi_Witty_ESP-12F1.GPIO2, Part1.SDA
  N5: Gizwits_WiFi_Witty_ESP-12F1.GPIO0, Part1.RST

custom parts:
  RFID-RC522-v2: A simple China made RFID-RC522 Reader; do check the pin labels, as this is a MFRC522 based clone.
